// Logisim project LogicAlarm.circ as structural Verilog: 10 circuits, main circuit main
module main (
  input  [2:0] in_1,
  input  in_2,
  input  in_3,
  input  in_4,
  input  [5:0] in_5,
  input  [5:0] in_6,
  input  [5:0] in_7,
  input  [5:0] in_8,
  input  [5:0] in_9,
  input  [5:0] in_10
);

  wire clk_div_1_f, clk_div_1_f_div_2, clk_div_1_f_div_4, clk_div_1_f_div_8, clk_div_1_f_div_16,
       clk_div_1_f_div_32, clk_div_1_f_div_64, clk_div_1_f_div_128, multiplexer_1_out;
  wire [5:0] hms24_1_h0, hms24_1_h1, hms24_1_m0, hms24_1_m1, hms24_1_s0, hms24_1_s1;
  wire [7:0] sixsegdriver_1_segout0, sixsegdriver_1_segout1, sixsegdriver_1_segout2, sixsegdriver_1_segout3,
       sixsegdriver_1_segout4, sixsegdriver_1_segout5;

  clk_div clk_div_1 (
    .f(clk_div_1_f), .f_div_2(clk_div_1_f_div_2), .f_div_4(clk_div_1_f_div_4), .f_div_8(clk_div_1_f_div_8),
    .f_div_16(clk_div_1_f_div_16), .f_div_32(clk_div_1_f_div_32), .f_div_64(clk_div_1_f_div_64),
    .f_div_128(clk_div_1_f_div_128));  // open: clk_in
  Multiplexer #(.select(3), .enable("false")) multiplexer_1 (
    .in0(clk_div_1_f), .in1(clk_div_1_f_div_2), .in2(clk_div_1_f_div_4), .in3(clk_div_1_f_div_8),
    .in4(clk_div_1_f_div_16), .in5(clk_div_1_f_div_32), .in6(clk_div_1_f_div_64), .in7(clk_div_1_f_div_128),
    .out(multiplexer_1_out), .sel(in_1));
  hms24 hms24_1 (
    .RST(in_2), .UP_DN(in_3), .CLK(multiplexer_1_out), .SET(in_4), .h1_set(in_5), .h0_set(in_6),
    .m1_set(in_7), .m0_set(in_8), .s1_set(in_9), .s0_set(in_10), .h1(hms24_1_h1), .h0(hms24_1_h0),
    .m1(hms24_1_m1), .m0(hms24_1_m0), .s1(hms24_1_s1), .s0(hms24_1_s0));
  sixSegDriver sixsegdriver_1 (
    .segIn5(hms24_1_h1), .segIn4(hms24_1_h0), .segIn3(hms24_1_m1), .segIn2(hms24_1_m0), .segIn1(hms24_1_s1),
    .segIn0(hms24_1_s0), .segOut5(sixsegdriver_1_segout5), .segOut4(sixsegdriver_1_segout4),
    .segOut3(sixsegdriver_1_segout3), .segOut2(sixsegdriver_1_segout2), .segOut1(sixsegdriver_1_segout1),
    .segOut0(sixsegdriver_1_segout0));
  _7_Segment_Display u_7_segment_display_1 (
    .g(sixsegdriver_1_segout5[6]), .f(sixsegdriver_1_segout5[5]), .a(sixsegdriver_1_segout5[0]),
    .b(sixsegdriver_1_segout5[1]), .e(sixsegdriver_1_segout5[4]), .d(sixsegdriver_1_segout5[3]),
    .c(sixsegdriver_1_segout5[2]), .dp(sixsegdriver_1_segout5[7]));
  _7_Segment_Display u_7_segment_display_2 (
    .g(sixsegdriver_1_segout4[6]), .f(sixsegdriver_1_segout4[5]), .a(sixsegdriver_1_segout4[0]),
    .b(sixsegdriver_1_segout4[1]), .e(sixsegdriver_1_segout4[4]), .d(sixsegdriver_1_segout4[3]),
    .c(sixsegdriver_1_segout4[2]), .dp(sixsegdriver_1_segout4[7]));
  _7_Segment_Display u_7_segment_display_3 (
    .g(sixsegdriver_1_segout3[6]), .f(sixsegdriver_1_segout3[5]), .a(sixsegdriver_1_segout3[0]),
    .b(sixsegdriver_1_segout3[1]), .e(sixsegdriver_1_segout3[4]), .d(sixsegdriver_1_segout3[3]),
    .c(sixsegdriver_1_segout3[2]), .dp(sixsegdriver_1_segout3[7]));
  _7_Segment_Display u_7_segment_display_4 (
    .g(sixsegdriver_1_segout1[6]), .f(sixsegdriver_1_segout1[5]), .a(sixsegdriver_1_segout1[0]),
    .b(sixsegdriver_1_segout1[1]), .e(sixsegdriver_1_segout1[4]), .d(sixsegdriver_1_segout1[3]),
    .c(sixsegdriver_1_segout1[2]), .dp(sixsegdriver_1_segout1[7]));
  _7_Segment_Display u_7_segment_display_5 (
    .g(sixsegdriver_1_segout2[6]), .f(sixsegdriver_1_segout2[5]), .a(sixsegdriver_1_segout2[0]),
    .b(sixsegdriver_1_segout2[1]), .e(sixsegdriver_1_segout2[4]), .d(sixsegdriver_1_segout2[3]),
    .c(sixsegdriver_1_segout2[2]), .dp(sixsegdriver_1_segout2[7]));
  _7_Segment_Display u_7_segment_display_6 (
    .g(sixsegdriver_1_segout0[6]), .f(sixsegdriver_1_segout0[5]), .a(sixsegdriver_1_segout0[0]),
    .b(sixsegdriver_1_segout0[1]), .e(sixsegdriver_1_segout0[4]), .d(sixsegdriver_1_segout0[3]),
    .c(sixsegdriver_1_segout0[2]), .dp(sixsegdriver_1_segout0[7]));
endmodule

module segDriver (
  input  B5,
  input  B4,
  input  B3,
  input  B2,
  input  B1,
  input  B0,
  output a,
  output b,
  output c,
  output d,
  output e,
  output f,
  output g,
  output decimal
);

  wire nand_1_out, nand_2_out, nand_3_out, nand_4_out, nand_5_out, nand_6_out, nand_7_out, nand_8_out,
       nand_9_out, nand_10_out, nand_11_out, nand_12_out, nand_13_out, nand_14_out, nand_15_out, nand_16_out,
       nand_17_out, nand_18_out, nand_19_out, nand_20_out, nand_21_out, nand_22_out, nand_23_out,
       nand_24_out, nand_25_out, nand_26_out, nand_27_out, nand_28_out, nand_29_out, nand_30_out,
       nand_31_out, nand_32_out, nand_33_out, nand_34_out, nand_35_out, nand_36_out, nand_37_out,
       nand_38_out, nand_39_out, nand_40_out, nand_41_out, nand_42_out, nand_43_out, nand_44_out,
       nand_45_out, nand_46_out, nand_47_out, nand_48_out, nand_49_out, nand_50_out, nand_51_out,
       nand_52_out, nand_53_out, nand_54_out, nand_55_out, nand_56_out, nand_57_out, nand_58_out,
       nand_59_out, nand_60_out, nand_61_out, nand_62_out, nand_63_out, nand_64_out, nand_65_out,
       nand_66_out, nand_67_out, nand_68_out, nand_69_out, nand_70_out, nand_71_out, nand_72_out,
       nand_73_out, nand_74_out, nand_75_out, nand_76_out, nand_77_out, nand_78_out, nand_79_out,
       nand_80_out, nand_81_out, nand_82_out, nand_83_out, nand_84_out, nand_85_out, nand_86_out,
       nand_87_out, nand_88_out, nand_89_out, nand_90_out, nand_91_out, nand_92_out, nand_93_out,
       nand_94_out, nand_95_out, nand_96_out, nand_97_out, nand_98_out, nand_99_out, nand_100_out,
       nand_101_out, nand_102_out, nand_103_out, nand_104_out, nand_105_out, nand_106_out, nand_107_out,
       nand_108_out, nand_109_out, nand_110_out, nand_111_out, nand_112_out, nand_113_out, nand_114_out,
       nand_115_out, nand_116_out, nand_117_out, nand_118_out, nand_119_out, nand_120_out, nand_121_out,
       nand_122_out, nand_123_out, nand_124_out, nand_125_out, nand_126_out, nand_127_out, nand_128_out,
       nand_129_out, nand_130_out, nand_131_out, nand_132_out, nand_133_out, nand_134_out, nand_135_out,
       nand_136_out, nand_137_out, nand_138_out, nand_139_out, nand_140_out, nand_141_out, nand_142_out,
       nand_143_out, nand_144_out, nand_145_out, nand_146_out, nand_147_out, nand_148_out, nand_149_out,
       nand_150_out, nand_151_out, nand_152_out, nand_153_out, nand_154_out, nand_155_out, nand_156_out,
       nand_157_out, nand_158_out, nand_159_out, nand_160_out, nand_161_out, nand_162_out, nand_163_out,
       nand_164_out, nand_165_out, nand_166_out, nand_167_out, nand_168_out;

  nand nand_1 (nand_1_out, B2, B2);
  nand nand_2 (nand_2_out, B1, B1);
  nand nand_3 (nand_3_out, B0, B0);
  nand nand_4 (nand_4_out, B4, B4);
  nand nand_5 (nand_5_out, B3, B3);
  nand nand_6 (nand_6_out, B4, B4);
  nand nand_7 (nand_7_out, B3, B3);
  nand nand_8 (nand_8_out, B4, B4);
  nand nand_9 (nand_9_out, B3, B3);
  nand nand_10 (nand_10_out, B4, B4);
  nand nand_11 (nand_11_out, B2, B2);
  nand nand_12 (nand_12_out, B1, B1);
  nand nand_13 (nand_13_out, B4, B4);
  nand nand_14 (nand_14_out, B0, B0);
  nand nand_15 (nand_15_out, B2, B2);
  nand nand_16 (nand_16_out, B0, B0);
  nand nand_17 (nand_17_out, B4, B4);
  nand nand_18 (nand_18_out, B3, B3);
  nand nand_19 (nand_19_out, B1, B1);
  nand nand_20 (nand_20_out, B0, B0);
  nand nand_21 (nand_21_out, B4, B4);
  nand nand_22 (nand_22_out, B2, B2);
  nand nand_23 (nand_23_out, B0, B0);
  nand nand_24 (nand_24_out, B3, B3);
  nand nand_25 (nand_25_out, B2, B2);
  nand nand_26 (nand_26_out, B3, B3);
  nand nand_27 (nand_27_out, B4, B4);
  nand nand_28 (nand_28_out, B1, B1);
  nand nand_29 (nand_29_out, B1, B1);
  nand nand_30 (nand_30_out, B0, B0);
  nand nand_31 (nand_31_out, B1, B1);
  nand nand_32 (nand_32_out, B4, B4);
  nand nand_33 (nand_33_out, B3, B3);
  nand nand_34 (nand_34_out, B1, B1);
  nand nand_35 (nand_35_out, B4, B4);
  nand nand_36 (nand_36_out, B3, B3);
  nand nand_37 (nand_37_out, B4, B4);
  nand nand_38 (nand_38_out, B3, B3);
  nand nand_39 (nand_39_out, B1, B1);
  nand nand_40 (nand_40_out, B4, B4);
  nand nand_41 (nand_41_out, B2, B2);
  nand nand_42 (nand_42_out, B3, B3);
  nand nand_43 (nand_43_out, B2, B2);
  nand nand_44 (nand_44_out, B2, B2);
  nand nand_45 (nand_45_out, B0, B0);
  nand nand_46 (nand_46_out, B3, B3);
  nand nand_47 (nand_47_out, B0, B0);
  nand nand_48 (nand_48_out, B1, B1);
  nand nand_49 (nand_49_out, B0, B0);
  nand nand_50 (nand_50_out, B4, B4);
  nand nand_51 (nand_51_out, B3, B3);
  nand nand_52 (nand_52_out, B2, B2);
  nand nand_53 (nand_53_out, B0, B0);
  nand nand_54 (nand_54_out, B3, B3);
  nand nand_55 (nand_55_out, B2, B2);
  nand nand_56 (nand_56_out, B4, B4);
  nand nand_57 (nand_57_out, B1, B1);
  nand nand_58 (nand_58_out, B4, B4);
  nand nand_59 (nand_59_out, B0, B0);
  nand nand_60 (nand_60_out, B4, B4);
  nand nand_61 (nand_61_out, B1, B1);
  nand nand_62 (nand_62_out, B4, B4);
  nand nand_63 (nand_63_out, B2, B2);
  nand nand_64 (nand_64_out, B1, B1);
  nand nand_65 (nand_65_out, B3, B3);
  nand nand_66 (nand_66_out, B1, B1);
  nand nand_67 (nand_67_out, B0, B0);
  nand nand_68 (nand_68_out, B3, B3);
  nand nand_69 (nand_69_out, B0, B0);
  nand nand_70 (nand_70_out, B2, B2);
  nand nand_71 (nand_71_out, B0, B0);
  nand nand_72 (nand_72_out, B4, B4);
  nand nand_73 (nand_73_out, B2, B2);
  nand nand_74 (nand_74_out, B0, B0);
  nand nand_75 (nand_75_out, B4, B4);
  nand nand_76 (nand_76_out, B0, B0);
  nand nand_77 (nand_77_out, B4, B4);
  nand nand_78 (nand_78_out, B4, B4);
  nand nand_79 (nand_79_out, B2, B2);
  nand nand_80 (nand_80_out, B3, B3);
  nand nand_81 (nand_81_out, B1, B1);
  nand nand_82 (nand_82_out, B0, B0);
  nand nand_83 (nand_83_out, B1, B1);
  nand nand_84 (nand_84_out, B0, B0);
  nand nand_85 (nand_85_out, B4, B4);
  nand nand_86 (nand_86_out, B3, B3);
  nand nand_87 (nand_87_out, B1, B1);
  nand nand_88 (nand_88_out, B4, B4);
  nand nand_89 (nand_89_out, B0, B0);
  nand nand_90 (nand_90_out, B4, B4);
  nand nand_91 (nand_91_out, B2, B2);
  nand nand_92 (nand_92_out, B4, B4);
  nand nand_93 (nand_93_out, B2, B2);
  nand nand_94 (nand_94_out, B3, B3);
  nand nand_95 (nand_95_out, B2, B2);
  nand nand_96 (nand_96_out, B1, B1);
  nand nand_97 (nand_97_out, B3, B3);
  nand nand_98 (nand_98_out, B1, B1);
  nand nand_99 (nand_99_out, B4, B4);
  nand nand_100 (nand_100_out, B2, B2);
  nand nand_101 (nand_101_out, B4, B4);
  nand nand_102 (nand_102_out, B3, B3);
  nand nand_103 (nand_103_out, B1, B1);
  nand nand_104 (nand_104_out, B1, B1);
  nand nand_105 (nand_105_out, B0, B0);
  nand nand_106 (nand_106_out, B2, B2);
  nand nand_107 (nand_107_out, B4, B4);
  nand nand_108 (nand_108_out, B2, B2);
  nand nand_109 (nand_109_out, B1, B1);
  nand nand_110 (nand_110_out, B3, B3);
  nand nand_111 (nand_111_out, nand_1_out, nand_2_out, nand_3_out);
  nand nand_112 (nand_112_out, nand_4_out, nand_5_out, B1);
  nand nand_113 (nand_113_out, nand_6_out, nand_7_out, B2, B0);
  nand nand_114 (nand_114_out, nand_8_out, B2, B1);
  nand nand_115 (nand_115_out, nand_9_out, B2, B1, B0);
  nand nand_116 (nand_116_out, nand_10_out, B3, nand_11_out, nand_12_out);
  nand nand_117 (nand_117_out, nand_13_out, B3, nand_14_out);
  nand nand_118 (nand_118_out, B3, nand_15_out, nand_16_out);
  nand nand_119 (nand_119_out, nand_17_out, nand_18_out, nand_19_out, nand_20_out);
  nand nand_120 (nand_120_out, nand_21_out, nand_22_out, nand_23_out);
  nand nand_121 (nand_121_out, nand_24_out, nand_25_out);
  nand nand_122 (nand_122_out, nand_26_out, B1, B0);
  nand nand_123 (nand_123_out, nand_27_out, B3, nand_28_out, B0);
  nand nand_124 (nand_124_out, B4, B3, nand_29_out, nand_30_out);
  nand nand_125 (nand_125_out, B4, B3, B2, nand_31_out);
  nand nand_126 (nand_126_out, nand_32_out, nand_33_out, nand_34_out);
  nand nand_127 (nand_127_out, nand_35_out, nand_36_out, B0);
  nand nand_128 (nand_128_out, nand_37_out, nand_38_out, B2);
  nand nand_129 (nand_129_out, B2, nand_39_out, B0);
  nand nand_130 (nand_130_out, nand_40_out, B3, nand_41_out);
  nand nand_131 (nand_131_out, B4, nand_42_out, nand_43_out);
  nand nand_132 (nand_132_out, B4, nand_44_out, nand_45_out);
  nand nand_133 (nand_133_out, B4, nand_46_out, B1, nand_47_out);
  nand nand_134 (nand_134_out, B4, B3, nand_48_out, nand_49_out);
  nand nand_135 (nand_135_out, nand_50_out, nand_51_out, nand_52_out, nand_53_out);
  nand nand_136 (nand_136_out, nand_54_out, nand_55_out, B1, B0);
  nand nand_137 (nand_137_out, nand_56_out, B2, nand_57_out, B0);
  nand nand_138 (nand_138_out, nand_58_out, B2, B1, nand_59_out);
  nand nand_139 (nand_139_out, nand_60_out, B3, nand_61_out);
  nand nand_140 (nand_140_out, nand_62_out, B3, nand_63_out, B0);
  nand nand_141 (nand_141_out, B3, B2, nand_64_out);
  nand nand_142 (nand_142_out, B4, nand_65_out, nand_66_out, nand_67_out);
  nand nand_143 (nand_143_out, B4, nand_68_out, B2, nand_69_out);
  nand nand_144 (nand_144_out, B4, B3, nand_70_out, B1, nand_71_out);
  nand nand_145 (nand_145_out, nand_72_out, nand_73_out, nand_74_out);
  nand nand_146 (nand_146_out, nand_75_out, B1, nand_76_out);
  nand nand_147 (nand_147_out, nand_77_out, B3, B1);
  nand nand_148 (nand_148_out, nand_78_out, B3, B2);
  nand nand_149 (nand_149_out, B4, nand_79_out, B0);
  nand nand_150 (nand_150_out, B4, nand_80_out, B2);
  nand nand_151 (nand_151_out, B4, B2, nand_81_out, nand_82_out);
  nand nand_152 (nand_152_out, nand_83_out, nand_84_out);
  nand nand_153 (nand_153_out, nand_85_out, nand_86_out, B2, nand_87_out);
  nand nand_154 (nand_154_out, nand_88_out, B2, nand_89_out);
  nand nand_155 (nand_155_out, nand_90_out, B3, nand_91_out);
  nand nand_156 (nand_156_out, nand_92_out, B3, B1);
  nand nand_157 (nand_157_out, B3, nand_93_out, B1);
  nand nand_158 (nand_158_out, B4, nand_94_out, nand_95_out, nand_96_out);
  nand nand_159 (nand_159_out, B4, nand_97_out, B2, B1, B0);
  nand nand_160 (nand_160_out, B4, B3, B2, nand_98_out);
  nand nand_161 (nand_161_out, nand_99_out, nand_100_out, B1);
  nand nand_162 (nand_162_out, nand_101_out, nand_102_out, B2, nand_103_out);
  nand nand_163 (nand_163_out, B2, nand_104_out, B0);
  nand nand_164 (nand_164_out, B2, B1, nand_105_out);
  nand nand_165 (nand_165_out, B3, nand_106_out);
  nand nand_166 (nand_166_out, nand_107_out, B3, B1);
  nand nand_167 (nand_167_out, B4, nand_108_out, nand_109_out);
  nand nand_168 (nand_168_out, B4, nand_110_out, B2, B1);
  nand nand_169 (a, nand_111_out, nand_112_out, nand_113_out, nand_114_out, nand_115_out, nand_116_out, nand_117_out, nand_118_out);
  nand nand_170 (b, nand_119_out, nand_120_out, nand_121_out, nand_122_out, nand_123_out, nand_124_out, nand_125_out);
  nand nand_171 (c, nand_126_out, nand_127_out, nand_128_out, nand_129_out, nand_130_out, nand_131_out, nand_132_out, nand_133_out, nand_134_out);
  nand nand_172 (d, nand_135_out, nand_136_out, nand_137_out, nand_138_out, nand_139_out, nand_140_out, nand_141_out, nand_142_out, nand_143_out, nand_144_out);
  nand nand_173 (e, nand_145_out, nand_146_out, nand_147_out, nand_148_out, nand_149_out, nand_150_out, nand_151_out);
  nand nand_174 (f, nand_152_out, nand_153_out, nand_154_out, nand_155_out, nand_156_out, nand_157_out, nand_158_out, nand_159_out, nand_160_out);
  nand nand_175 (g, nand_161_out, nand_162_out, nand_163_out, nand_164_out, nand_165_out, nand_166_out, nand_167_out, nand_168_out);

  assign decimal = B5;
endmodule

module sixSegDriver (
  input  [5:0] segIn5,
  input  [5:0] segIn4,
  input  [5:0] segIn3,
  input  [5:0] segIn2,
  input  [5:0] segIn1,
  input  [5:0] segIn0,
  output [7:0] segOut5,
  output [7:0] segOut4,
  output [7:0] segOut3,
  output [7:0] segOut2,
  output [7:0] segOut1,
  output [7:0] segOut0
);

  segDriverSplit segdriversplit_1 (.segIn(segIn5), .segOut(segOut5));
  segDriverSplit segdriversplit_2 (.segIn(segIn4), .segOut(segOut4));
  segDriverSplit segdriversplit_3 (.segIn(segIn3), .segOut(segOut3));
  segDriverSplit segdriversplit_4 (.segIn(segIn2), .segOut(segOut2));
  segDriverSplit segdriversplit_5 (.segIn(segIn1), .segOut(segOut1));
  segDriverSplit segdriversplit_6 (.segIn(segIn0), .segOut(segOut0));
endmodule

module segDriverSplit (
  input  [5:0] segIn,
  output [7:0] segOut
);

  segDriver segdriver_1 (
    .B5(segIn[5]), .B4(segIn[4]), .B3(segIn[3]), .B2(segIn[2]), .B1(segIn[1]), .B0(segIn[0]), .a(segOut[0]),
    .b(segOut[1]), .c(segOut[2]), .d(segOut[3]), .e(segOut[4]), .f(segOut[5]), .g(segOut[6]),
    .decimal(segOut[7]));
endmodule

module base_6_count (
  input  RST,
  input  UP_DN,
  input  CIN,
  input  SET,
  input  [5:0] SVAL,
  output COUT,
  output [5:0] VAL
);

  wire counter_1_carry, not_1_out;

  not not_1 (not_1_out, UP_DN);
  Counter #(.width(6), .max('h5)) counter_1 (
    .clr(RST), .load(SET), .up(not_1_out), .clk(CIN), .D(SVAL), .carry(counter_1_carry), .Q(VAL));  // open: count
  D_Flip_Flop d_ff_1 (.D(counter_1_carry), .clk(CIN), .Q(COUT), .preset(SET), .reset(RST));  // open: Qn
endmodule

module base_10_count (
  input  RST,
  input  UP_DN,
  input  CIN,
  input  SET,
  input  [5:0] SVAL,
  output COUT,
  output [5:0] VAL
);

  wire counter_1_carry, multiplexer_1_out, not_1_out;

  not not_1 (not_1_out, UP_DN);
  Multiplexer #(.enable("false")) multiplexer_1 (.in0(CIN), .in1(1'b1), .out(multiplexer_1_out), .sel(SET));
  Counter #(.width(6), .max('h9)) counter_1 (
    .clr(RST), .load(SET), .up(not_1_out), .clk(multiplexer_1_out), .D(SVAL), .carry(counter_1_carry), .Q(VAL));  // open: count
  D_Flip_Flop d_ff_1 (.D(counter_1_carry), .clk(multiplexer_1_out), .Q(COUT), .preset(SET), .reset(RST));  // open: Qn
endmodule

module hms24 (
  input  RST,
  input  UP_DN,
  input  CLK,
  input  SET,
  input  [5:0] h1_set,
  input  [5:0] h0_set,
  input  [5:0] m1_set,
  input  [5:0] m0_set,
  input  [5:0] s1_set,
  input  [5:0] s0_set,
  output [5:0] h1,
  output [5:0] h0,
  output [5:0] m1,
  output [5:0] m0,
  output [5:0] s1,
  output [5:0] s0
);

  wire base_4_count_1_cout, base_6_count_1_cout, base_6_count_2_cout, base_10_count_1_cout,
       base_10_count_2_cout;

  base_3_count base_3_count_1 (
    .RST(RST), .UP_DN(UP_DN), .CIN(base_4_count_1_cout), .SET(SET), .SVAL(h1_set), .VAL(h1));  // open: COUT
  base_4_count base_4_count_1 (
    .RST(RST), .UP_DN(UP_DN), .CIN(base_6_count_1_cout), .SET(SET), .SVAL(h0_set),
    .COUT(base_4_count_1_cout), .VAL(h0));
  base_6_count base_6_count_1 (
    .RST(RST), .UP_DN(UP_DN), .CIN(base_10_count_1_cout), .SET(SET), .SVAL(m1_set),
    .COUT(base_6_count_1_cout), .VAL(m1));
  base_10_count base_10_count_1 (
    .RST(RST), .UP_DN(UP_DN), .CIN(base_6_count_2_cout), .SET(SET), .SVAL(m0_set),
    .COUT(base_10_count_1_cout), .VAL(m0));
  base_6_count base_6_count_2 (
    .RST(RST), .UP_DN(UP_DN), .CIN(base_10_count_2_cout), .SET(SET), .SVAL(s1_set),
    .COUT(base_6_count_2_cout), .VAL(s1));
  base_10_count base_10_count_2 (
    .RST(RST), .UP_DN(UP_DN), .CIN(CLK), .SET(SET), .SVAL(s0_set), .COUT(base_10_count_2_cout), .VAL(s0));
endmodule

module base_4_count (
  input  RST,
  input  UP_DN,
  input  CIN,
  input  SET,
  input  [5:0] SVAL,
  output COUT,
  output [5:0] VAL
);

  wire counter_1_carry, not_1_out;

  not not_1 (not_1_out, UP_DN);
  Counter #(.width(6), .max('h3)) counter_1 (
    .clr(RST), .load(SET), .up(not_1_out), .clk(CIN), .D(SVAL), .carry(counter_1_carry), .Q(VAL));  // open: count
  D_Flip_Flop d_ff_1 (.D(counter_1_carry), .clk(CIN), .Q(COUT), .preset(SET), .reset(RST));  // open: Qn
endmodule

module base_3_count (
  input  RST,
  input  UP_DN,
  input  CIN,
  input  SET,
  input  [5:0] SVAL,
  output COUT,
  output [5:0] VAL
);

  wire counter_1_carry, not_1_out;

  not not_1 (not_1_out, UP_DN);
  Counter #(.width(6), .max('h2)) counter_1 (
    .clr(RST), .load(SET), .up(not_1_out), .clk(CIN), .D(SVAL), .carry(counter_1_carry), .Q(VAL));  // open: count
  D_Flip_Flop d_ff_1 (.D(counter_1_carry), .clk(CIN), .Q(COUT), .preset(SET), .reset(RST));  // open: Qn
endmodule

module clk_div (
  input  clk_in,
  output f,
  output f_div_2,
  output f_div_4,
  output f_div_8,
  output f_div_16,
  output f_div_32,
  output f_div_64,
  output f_div_128
);

  wire d_ff_1_qn, d_ff_2_qn, d_ff_3_qn, d_ff_4_qn, d_ff_5_qn, d_ff_6_qn, d_ff_7_qn;

  not not_1 (f, clk_in);
  D_Flip_Flop d_ff_1 (.D(d_ff_1_qn), .clk(clk_in), .Q(f_div_2), .Qn(d_ff_1_qn));  // open: preset, reset
  D_Flip_Flop d_ff_2 (.D(d_ff_2_qn), .clk(d_ff_1_qn), .Q(f_div_4), .Qn(d_ff_2_qn));  // open: preset, reset
  D_Flip_Flop d_ff_3 (.D(d_ff_3_qn), .clk(d_ff_2_qn), .Q(f_div_8), .Qn(d_ff_3_qn));  // open: preset, reset
  D_Flip_Flop d_ff_4 (.D(d_ff_4_qn), .clk(d_ff_3_qn), .Q(f_div_16), .Qn(d_ff_4_qn));  // open: preset, reset
  D_Flip_Flop d_ff_5 (.D(d_ff_5_qn), .clk(d_ff_4_qn), .Q(f_div_32), .Qn(d_ff_5_qn));  // open: preset, reset
  D_Flip_Flop d_ff_6 (.D(d_ff_6_qn), .clk(d_ff_5_qn), .Q(f_div_64), .Qn(d_ff_6_qn));  // open: preset, reset
  D_Flip_Flop d_ff_7 (.D(d_ff_7_qn), .clk(d_ff_6_qn), .Q(f_div_128), .Qn(d_ff_7_qn));  // open: preset, reset
endmodule
